# Fritzing sketch schematics (saved by Fritzing 0.9.2b)
breadboards: 1

parts:
  Part1 = Arduino Uno (Rev3)
  DHT22 = DHT22 Humidity and Temperature Sensor
  R1 = Resistor [tolerance=±5% resistance=10k package=THT]
  BMP_180 = Barometric Pressure Sensor - BMP180 Breakout (GY-68)  # not connected
  Part2 = Matrix LED de 8x8 basada en MAX7219

nets:
  N1: Part1.D8, Part2.CS
  N2: Part1.D9_PWM, Part2.CLK
  N3: Part1.D10_PWM/SS, Part2.DIN
  N4: Part1.D7, DHT22.DATA, R1.Pin_0
  5V: Part1.5V, DHT22.VDD, R1.Pin_1, Part2.VCC
  GND: Part1.GND, DHT22.GND, Part2.GND
